// Logisim project Ejemplo 1.circ as structural Verilog: 5 circuits, main circuit NOT
module NOT (
  input  in_1,
  output out_2
);

  Transistor #(.\type ("n")) transistor_1 (.in(1'b0), .out(out_2), .gate(in_1));
  Transistor transistor_2 (.in(1'b1), .out(out_2), .gate(in_1));

  // Notes on the sheet:
  //   N
  //   P
endmodule

module NOT_PULL (
  input  in_1,
  output out_2
);

  Transistor #(.\type ("n")) transistor_1 (.in(1'b0), .out(out_2), .gate(in_1));
  Pull_Resistor #(.pull(1)) pull_resistor_1 (.node(out_2));

  // Notes on the sheet:
  //   N
endmodule

module AND (
  input  in_1,
  input  in_2,
  output out_3
);

  Transistor #(.\type ("n")) transistor_1 (.in(in_1), .out(out_3), .gate(in_2));
  Transistor transistor_2 (.in(in_2), .out(out_3), .gate(in_2));

  // Notes on the sheet:
  //   N
  //   P
endmodule

module OR (
  input  in_1,
  input  in_2,
  output out_3
);

  Transistor transistor_1 (.in(in_1), .out(out_3), .gate(in_2));
  Transistor #(.\type ("n")) transistor_2 (.in(in_2), .out(out_3), .gate(in_2));

  // Notes on the sheet:
  //   N
  //   P
endmodule

module Ejemplo (
  input  A,
  input  B,
  input  C,
  input  D,
  output F1,
  output F2,
  output F3
);

  wire A_nB_nCD_out, AB_nC_nD_out, ABCD_out, nA_nBCD_out, nABC_nD_out, not_1_out, not_2_out, not_3_out,
       not_4_out;

  not not_1 (not_1_out, A);
  not not_2 (not_2_out, B);
  not not_3 (not_3_out, C);
  not not_4 (not_4_out, D);
  or or_1 (F1, AB_nC_nD_out, ABCD_out);
  and AB_nC_nD (AB_nC_nD_out, A, B, not_3_out, not_4_out);
  and ABCD (ABCD_out, A, B, C, D);
  and nABC_nD (nABC_nD_out, not_1_out, B, C, not_4_out);
  and A_nB_nCD (A_nB_nCD_out, A, not_2_out, not_3_out, D);
  and nA_nBCD (nA_nBCD_out, not_1_out, not_2_out, C, D);
  or or_2 (F2, nABC_nD_out, A_nB_nCD_out);
  or or_3 (F3, nA_nBCD_out, A_nB_nCD_out, ABCD_out);
endmodule
