// Logisim project Ejemplo 2 - Practica 03.circ as structural Verilog: 1 circuit, main circuit ALU 1 bit
module ALU_1_bit (
  input  Selector,
  input  A,
  input  B,
  output R
);

  wire and_1_out, or_1_out;

  and and_1 (and_1_out, A, B);
  or or_1 (or_1_out, A, B);
  Multiplexer #(.enable("false")) multiplexer_1 (.in0(and_1_out), .in1(or_1_out), .out(R), .sel(Selector));
endmodule
