// Logisim project Ejemplo 3 - Práctica 4.circ as structural Verilog: 2 circuits, main circuit Circuito secuencial
module Circuito_combinacional (
  input  E1,
  input  E2,
  input  A,
  input  B,
  output E1_2,
  output E2_2
);

  wire and_1_out, and_2_out, and_3_out, and_4_out, and_5_out, not_1_out, not_2_out, not_3_out, not_4_out;

  not not_1 (not_1_out, E1);
  not not_2 (not_2_out, E2);
  not not_3 (not_3_out, A);
  not not_4 (not_4_out, B);
  and and_1 (and_1_out, not_3_out, not_4_out);
  and and_2 (and_2_out, E2, B);
  and and_3 (and_3_out, not_1_out, not_3_out, not_4_out);
  and and_4 (and_4_out, not_1_out, not_2_out, not_4_out);
  and and_5 (and_5_out, E1, A, B);
  or or_1 (E1_2, E1, and_1_out);
  or or_2 (E2_2, and_2_out, and_3_out, and_4_out, and_5_out);
endmodule

module Circuito_secuencial (
  input  [1:0] A_B,
  input  Clock
);

  wire circuito_combinacional_1_e1_2, circuito_combinacional_1_e2_2, E1_q, E2_q;

  Circuito_combinacional circuito_combinacional_1 (
    .E1(E1_q), .E2(E2_q), .A(A_B[0]), .B(A_B[1]), .E1_2(circuito_combinacional_1_e1_2),
    .E2_2(circuito_combinacional_1_e2_2));
  D_Flip_Flop E1 (.clk(Clock), .D(circuito_combinacional_1_e1_2), .Q(E1_q));  // open: Qn, preset, en, reset
  D_Flip_Flop E2 (.clk(Clock), .D(circuito_combinacional_1_e2_2), .Q(E2_q));  // open: Qn, preset, en, reset

  // Notes on the sheet:
  //   Entrada
  //   Circuito Combinacional
  //   Memoria
endmodule
