// Logisim project practica02.circ as structural Verilog: 4 circuits, main circuit Implicacion
module Implicacion (
  input  p,
  input  q,
  output out_3
);

  wire transistor_1_out;

  Transistor #(.\type ("n")) transistor_1 (.in(1'b0), .out(transistor_1_out), .gate(p));
  Transistor transistor_2 (.in(1'b1), .out(transistor_1_out), .gate(p));
  Transistor #(.\type ("n")) transistor_3 (.in(transistor_1_out), .out(out_3), .gate(transistor_1_out));
  Transistor transistor_4 (.in(q), .out(out_3), .gate(transistor_1_out));

  // Notes on the sheet:
  //   N
  //   ¬p
  //   P
  //   P->Q <=> ¬PvQ
  //   P
  //   N
  //   NOT
  //   OR
endmodule

module Numeros_Primos (
  input  A,
  input  B,
  input  C,
  output out_4
);

  wire AC_out, nAB_out, not_1_out;

  not not_1 (not_1_out, A);
  and AC (AC_out, A, C);
  and nAB (nAB_out, not_1_out, B);
  or or_1 (out_4, AC_out, nAB_out);

  // Notes on the sheet:
  //   0(No es primo)/1(Es primo)
endmodule

module Menor_o_Igual (
  input  A,
  input  B,
  input  C,
  input  D,
  output x_y,
  output x_y_2
);

  wire A_nBC_nD_out, ABCD_out, nA_nB_nC_nD_out, nA_nBD_out, \nAB_nCÐ_out , nAC_out, nBCD_out, not_1_out,
       not_2_out, not_3_out, not_4_out;

  not not_1 (not_1_out, A);
  not not_2 (not_2_out, B);
  not not_3 (not_3_out, C);
  not not_4 (not_4_out, D);
  and nA_nBD (nA_nBD_out, not_1_out, not_2_out, D);
  and nAC (nAC_out, not_1_out, C);
  and nBCD (nBCD_out, not_2_out, C, D);
  and nA_nB_nC_nD (nA_nB_nC_nD_out, not_1_out, not_2_out, not_3_out, not_4_out);
  and \nAB_nCÐ  (\nAB_nCÐ_out , not_1_out, B, not_3_out, D);
  and ABCD (ABCD_out, A, B, C, D);
  and A_nBC_nD (A_nBC_nD_out, A, not_2_out, C, not_4_out);
  or or_1 (x_y, nA_nBD_out, nAC_out, nBCD_out);
  or or_2 (x_y_2, nA_nB_nC_nD_out, \nAB_nCÐ_out , ABCD_out, A_nBC_nD_out);

  // Notes on the sheet:
  //   X
  //   Y
  //   x<y
  //   x=y
endmodule

module Elevador (
  input  A,
  input  B,
  input  C,
  input  D,
  output out_5,
  output \Número_de_pisos ,
  output out_7
);

  wire A_nC_nD_out, AB_nC_out, B_nD_out, nA_nBC_out, nA_nBD_out, nAC_out, nACD_out, nBCD_out, nBD_out,
       not_1_out, not_2_out, not_3_out, not_4_out;

  not not_1 (not_1_out, A);
  not not_2 (not_2_out, B);
  not not_3 (not_3_out, C);
  not not_4 (not_4_out, D);
  and nA_nBD (nA_nBD_out, not_1_out, not_2_out, D);
  and nAC (nAC_out, not_1_out, C);
  and nBCD (nBCD_out, not_2_out, C, D);
  and A_nC_nD (A_nC_nD_out, A, not_3_out, not_4_out);
  and AB_nC (AB_nC_out, A, B, not_3_out);
  and nACD (nACD_out, not_1_out, C, D);
  and nA_nBC (nA_nBC_out, not_1_out, not_2_out, C);
  and B_nD (B_nD_out, B, not_4_out);
  and nBD (nBD_out, not_2_out, D);
  or or_1 (out_5, nA_nBD_out, nAC_out, nBCD_out);
  or or_2 (\Número_de_pisos , A_nC_nD_out, AB_nC_out, nACD_out, nA_nBC_out);
  or or_3 (out_7, B_nD_out, nBD_out);

  // Notes on the sheet:
  //   PISO ACTUAL
  //   PISO SELECCIONADO
  //   Dirección
  //   Primer bit del numero binario
  //   Segundo bit del numero binario
  //   0(ABAJO)/1(ARRIBA)
endmodule
