// Logisim project Sumador.circ as structural Verilog: 1 circuit, main circuit main
module main (
  input  A,
  input  B,
  input  Op,
  input  Ci,
  output S,
  output C_i_1
);

  wire and_1_out, and_2_out, xor_1_out, xor_2_out;

  and and_1 (and_1_out, A, B);
  and and_2 (and_2_out, Ci, xor_1_out);
  // AND_Gate and_3 has open pins: in0=B, in4=A, out=open
  // OR_Gate or_1 has open pins: in0=A, in4=B, out=open
  xor xor_1 (xor_1_out, A, B);
  Multiplexer #(.enable("false")) multiplexer_1 (.in1(xor_2_out), .sel(Op));  // open: in0, out
  xor xor_2 (xor_2_out, xor_1_out, Ci);
  or or_2 (C_i_1, and_2_out, and_1_out);

  // Notes on the sheet:
  //   Sumador Completo
  //   2^n entradas
  //   salida
  //   n seleccion
  //   Salida
endmodule
