// Logisim project Combinacional.circ as structural Verilog: 8 circuits, main circuit ALU de 1 bit (Sumador)
module ALU_de_1_bit__Sumador (
  input  A,
  input  B,
  input  [2:0] Op,
  input  C_i,
  output S,
  output C_i_1
);

  wire A___B_____C_i_out, A___B_out, A_B_out, AB_2_out, AB_out, C_i___A___B_out;

  and AB (AB_out, A, B);
  and C_i___A___B (C_i___A___B_out, C_i, A___B_out);
  and AB_2 (AB_2_out, B, A);
  or A_B (A_B_out, A, B);
  xor A___B (A___B_out, A, B);
  Multiplexer #(.select(3), .enable("false")) multiplexer_1 (
    .in0(AB_2_out), .in1(A_B_out), .in4(A___B_____C_i_out), .out(S), .sel(Op));  // open: in2, in3, in5, in6, in7
  xor A___B_____C_i (A___B_____C_i_out, A___B_out, C_i);
  or AB__C_i___A___B (C_i_1, C_i___A___B_out, AB_out);

  // Notes on the sheet:
  //   Sumador Completo
  //   2^n entradas
  //   salida
  //   n seleccion
  //   Salida
  //   Acarreo
endmodule

module ALU_8_bits__Sumador (
  input  in_1,
  input  [2:0] Op,
  input  A,
  input  B,
  input  A_2,
  input  B_2,
  input  A_3,
  input  B_3,
  input  A_4,
  input  B_4,
  input  A_5,
  input  B_5,
  input  A_6,
  input  B_6,
  input  A_7,
  input  B_7,
  input  A_8,
  input  B_8,
  output out_19,
  output out_20,
  output out_21,
  output out_22,
  output out_23,
  output out_24,
  output out_25,
  output out_26,
  output out_27
);

  wire alu_de_1_bit_sumador_1_c_i_1, alu_de_1_bit_sumador_2_c_i_1, alu_de_1_bit_sumador_3_c_i_1,
       alu_de_1_bit_sumador_4_c_i_1, alu_de_1_bit_sumador_5_c_i_1, alu_de_1_bit_sumador_6_c_i_1,
       alu_de_1_bit_sumador_7_c_i_1;

  ALU_de_1_bit__Sumador alu_de_1_bit_sumador_1 (
    .A(A), .B(B), .Op(Op), .C_i(in_1), .S(out_19), .C_i_1(alu_de_1_bit_sumador_1_c_i_1));
  ALU_de_1_bit__Sumador alu_de_1_bit_sumador_2 (
    .A(A_2), .B(B_2), .Op(Op), .C_i(alu_de_1_bit_sumador_1_c_i_1), .S(out_20),
    .C_i_1(alu_de_1_bit_sumador_2_c_i_1));
  ALU_de_1_bit__Sumador alu_de_1_bit_sumador_3 (
    .A(A_3), .B(B_3), .Op(Op), .C_i(alu_de_1_bit_sumador_2_c_i_1), .S(out_21),
    .C_i_1(alu_de_1_bit_sumador_3_c_i_1));
  ALU_de_1_bit__Sumador alu_de_1_bit_sumador_4 (
    .A(A_4), .B(B_4), .Op(Op), .C_i(alu_de_1_bit_sumador_3_c_i_1), .S(out_22),
    .C_i_1(alu_de_1_bit_sumador_4_c_i_1));
  ALU_de_1_bit__Sumador alu_de_1_bit_sumador_5 (
    .A(A_5), .B(B_5), .Op(Op), .C_i(alu_de_1_bit_sumador_4_c_i_1), .S(out_23),
    .C_i_1(alu_de_1_bit_sumador_5_c_i_1));
  ALU_de_1_bit__Sumador alu_de_1_bit_sumador_6 (
    .A(A_6), .B(B_6), .Op(Op), .C_i(alu_de_1_bit_sumador_5_c_i_1), .S(out_24),
    .C_i_1(alu_de_1_bit_sumador_6_c_i_1));
  ALU_de_1_bit__Sumador alu_de_1_bit_sumador_7 (
    .A(A_7), .B(B_7), .Op(Op), .C_i(alu_de_1_bit_sumador_6_c_i_1), .S(out_25),
    .C_i_1(alu_de_1_bit_sumador_7_c_i_1));
  ALU_de_1_bit__Sumador alu_de_1_bit_sumador_8 (
    .A(A_8), .B(B_8), .Op(Op), .C_i(alu_de_1_bit_sumador_7_c_i_1), .S(out_26), .C_i_1(out_27));

  // Notes on the sheet:
  //   B
  //   Desbordamiento aritmetico
endmodule

module \ALU_de_1_bit__Sustracción  (
  input  A,
  input  B,
  input  [2:0] Op,
  input  C_i,
  output S,
  output C_i_1
);

  wire A___B___C_i_out, and_1_out, and_2_out, and_3_out, C_i_B_out, nAB_out, nAC_i_out, not_1_out, or_1_out,
       or_2_out, or_3_out, xor_1_out, xor_2_out;

  not not_1 (not_1_out, A);
  and and_1 (and_1_out, A, B);
  and nAB (nAB_out, not_1_out, B);
  and nAC_i (nAC_i_out, not_1_out, C_i);
  and and_2 (and_2_out, C_i, xor_1_out);
  and C_i_B (C_i_B_out, C_i, B);
  and and_3 (and_3_out, B, A);
  or or_1 (or_1_out, A, B);
  xor xor_1 (xor_1_out, A, B);
  Multiplexer #(.select(3), .enable("false")) multiplexer_1 (
    .in0(and_3_out), .in1(or_1_out), .in4(xor_2_out), .in5(A___B___C_i_out), .out(S), .sel(Op));  // open: in2, in3, in6, in7
  xor xor_2 (xor_2_out, xor_1_out, C_i);
  or or_2 (or_2_out, and_2_out, and_1_out);
  Multiplexer #(.select(3), .enable("false")) multiplexer_2 (
    .in4(or_2_out), .in5(or_3_out), .out(C_i_1), .sel(Op));  // open: in0, in1, in2, in3, in6, in7
  ExactlyOne A___B___C_i (.out(A___B___C_i_out), .in0(C_i), .in2(B), .in4(A));
  or or_3 (or_3_out, C_i_B_out, nAC_i_out, nAB_out);

  // Notes on the sheet:
  //   Sustraendo = B
  //   Minuendo = A
  //   Sumador Completo
  //   Restador Completo
  //   Bit prestado = C(i)
  //   2^n entradas
  //   salida
  //   n seleccion
  //   Salida
  //   Diferencia
  //   Prestamo
endmodule

module \ALU_8_bits__Sustracción  (
  input  in_1,
  input  [2:0] Op,
  input  in_3,
  input  in_4,
  input  in_5,
  input  in_6,
  input  in_7,
  input  in_8,
  input  in_9,
  input  in_10,
  input  in_11,
  input  in_12,
  input  in_13,
  input  in_14,
  input  in_15,
  input  in_16,
  input  in_17,
  input  in_18,
  output out_19,
  output out_20,
  output out_21,
  output out_22,
  output out_23,
  output out_24,
  output out_25,
  output out_26,
  output out_27,
  output out_28
);

  wire \alu_de_1_bit_sustracción_con_igualdad_1_s , \alu_de_1_bit_sustracción_con_igualdad_2_s ,
       \alu_de_1_bit_sustracción_con_igualdad_3_s , \alu_de_1_bit_sustracción_con_igualdad_4_s ,
       \alu_de_1_bit_sustracción_con_igualdad_5_s , \alu_de_1_bit_sustracción_con_igualdad_6_s ,
       \alu_de_1_bit_sustracción_con_igualdad_7_s ;

  \ALU_de_1_bit__Sustracción_con_igualdad  \alu_de_1_bit_sustracción_con_igualdad_1  (
    .A(in_3), .B(in_4), .Op(Op), .Ci(in_1), .S(\alu_de_1_bit_sustracción_con_igualdad_1_s ), .C_i_1(out_19));
  \ALU_de_1_bit__Sustracción_con_igualdad  \alu_de_1_bit_sustracción_con_igualdad_2  (
    .A(in_5), .B(in_6), .Op(Op), .Ci(\alu_de_1_bit_sustracción_con_igualdad_1_s ),
    .S(\alu_de_1_bit_sustracción_con_igualdad_2_s ), .C_i_1(out_20));
  \ALU_de_1_bit__Sustracción_con_igualdad  \alu_de_1_bit_sustracción_con_igualdad_3  (
    .A(in_7), .B(in_8), .Op(Op), .Ci(\alu_de_1_bit_sustracción_con_igualdad_2_s ),
    .S(\alu_de_1_bit_sustracción_con_igualdad_3_s ), .C_i_1(out_21));
  \ALU_de_1_bit__Sustracción_con_igualdad  \alu_de_1_bit_sustracción_con_igualdad_4  (
    .A(in_9), .B(in_10), .Op(Op), .Ci(\alu_de_1_bit_sustracción_con_igualdad_3_s ),
    .S(\alu_de_1_bit_sustracción_con_igualdad_4_s ), .C_i_1(out_22));
  \ALU_de_1_bit__Sustracción_con_igualdad  \alu_de_1_bit_sustracción_con_igualdad_5  (
    .A(in_11), .B(in_12), .Op(Op), .Ci(\alu_de_1_bit_sustracción_con_igualdad_4_s ),
    .S(\alu_de_1_bit_sustracción_con_igualdad_5_s ), .C_i_1(out_24));
  \ALU_de_1_bit__Sustracción_con_igualdad  \alu_de_1_bit_sustracción_con_igualdad_6  (
    .A(in_13), .B(in_14), .Op(Op), .Ci(\alu_de_1_bit_sustracción_con_igualdad_5_s ),
    .S(\alu_de_1_bit_sustracción_con_igualdad_6_s ), .C_i_1(out_25));
  \ALU_de_1_bit__Sustracción_con_igualdad  \alu_de_1_bit_sustracción_con_igualdad_7  (
    .A(in_15), .B(in_16), .Op(Op), .Ci(\alu_de_1_bit_sustracción_con_igualdad_6_s ),
    .S(\alu_de_1_bit_sustracción_con_igualdad_7_s ), .C_i_1(out_26));
  \ALU_de_1_bit__Sustracción_con_igualdad  \alu_de_1_bit_sustracción_con_igualdad_8  (
    .A(in_17), .B(in_18), .Op(Op), .Ci(\alu_de_1_bit_sustracción_con_igualdad_7_s ), .S(out_28),
    .C_i_1(out_27));
  and and_1 (out_23, out_19, out_20, out_21, out_22, out_24, out_25, out_26, out_27);

  // Notes on the sheet:
  //   Desbordamiento aritmetico
  //   0 no son iguales/ 1 son iguales
endmodule

module \ALU_de_1_bit__Sustracción_con_igualdad  (
  input  A,
  input  B,
  input  [2:0] Op,
  input  Ci,
  output S,
  output C_i_1
);

  wire A___B_out, and_1_out, and_2_out, and_3_out, and_4_out, and_5_out, and_6_out, not_1_out, not_2_out,
       or_1_out, or_2_out, or_3_out, xor_1_out, xor_2_out, xor_3_out;

  not not_1 (not_1_out, A);
  and and_1 (and_1_out, A, B);
  and and_2 (and_2_out, not_1_out, B);
  and and_3 (and_3_out, not_1_out, Ci);
  and and_4 (and_4_out, Ci, xor_1_out);
  and and_5 (and_5_out, Ci, B);
  and and_6 (and_6_out, B, A);
  or or_1 (or_1_out, A, B);
  xor xor_1 (xor_1_out, A, B);
  Multiplexer #(.select(3), .enable("false")) multiplexer_1 (
    .in0(and_6_out), .in1(or_1_out), .in3(not_2_out), .in4(xor_2_out), .in5(xor_3_out), .out(S), .sel(Op));  // open: in2, in6, in7
  xor xor_2 (xor_2_out, xor_1_out, Ci);
  or or_2 (or_2_out, and_4_out, and_1_out);
  xor A___B (A___B_out, A, B);
  Multiplexer #(.select(3), .enable("false")) multiplexer_2 (
    .in4(or_2_out), .in5(or_3_out), .out(C_i_1), .sel(Op));  // open: in0, in1, in2, in3, in6, in7
  ExactlyOne xor_3 (.out(xor_3_out), .in0(Ci), .in2(B), .in4(A));
  or or_3 (or_3_out, and_5_out, and_3_out, and_2_out);
  not not_2 (not_2_out, A___B_out);

  // Notes on the sheet:
  //   Sumador Completo
  //   Igualdad
  //   Restador Completo
  //   2^n entradas
  //   salida
  //   n seleccion
  //   Salida
endmodule

module ALU_de_1_bit__NOR (
  input  A,
  input  B,
  input  [2:0] Op,
  input  Ci,
  output S,
  output C_i_1
);

  wire and_1_out, and_2_out, and_3_out, and_4_out, and_5_out, and_6_out, nA_nB_out, not_1_out, not_2_out,
       not_3_out, not_4_out, or_1_out, or_2_out, or_3_out, xor_1_out, xor_2_out, xor_3_out, xor_4_out;

  not not_1 (not_1_out, A);
  and and_1 (and_1_out, A, B);
  and and_2 (and_2_out, not_1_out, B);
  and and_3 (and_3_out, not_1_out, Ci);
  and and_4 (and_4_out, Ci, xor_1_out);
  and and_5 (and_5_out, Ci, B);
  not not_2 (not_2_out, A);
  not not_3 (not_3_out, B);
  and and_6 (and_6_out, B, A);
  or or_1 (or_1_out, A, B);
  xor xor_1 (xor_1_out, A, B);
  and nA_nB (nA_nB_out, not_2_out, not_3_out);
  Multiplexer #(.select(3), .enable("false")) multiplexer_1 (
    .in0(and_6_out), .in1(or_1_out), .in2(nA_nB_out), .in3(not_4_out), .in4(xor_2_out), .in5(xor_4_out),
    .out(S), .sel(Op));  // open: in6, in7
  xor xor_2 (xor_2_out, xor_1_out, Ci);
  or or_2 (or_2_out, and_4_out, and_1_out);
  xor xor_3 (xor_3_out, A, B);
  Multiplexer #(.select(3), .enable("false")) multiplexer_2 (
    .in4(or_2_out), .in5(or_3_out), .out(C_i_1), .sel(Op));  // open: in0, in1, in2, in3, in6, in7
  ExactlyOne xor_4 (.out(xor_4_out), .in0(Ci), .in2(B), .in4(A));
  or or_3 (or_3_out, and_5_out, and_3_out, and_2_out);
  not not_4 (not_4_out, xor_3_out);

  // Notes on the sheet:
  //   Sumador Completo
  //   Restador Completo
  //   NOR
  //   2^n entradas
  //   salida
  //   n seleccion
  //   Salida
  //   Igualdad
endmodule

module ALU_8_bits_Final (
  input  in_1,
  input  [2:0] in_2,
  input  in_3,
  input  in_4,
  input  in_5,
  input  in_6,
  input  in_7,
  input  in_8,
  input  in_9,
  input  in_10,
  input  in_11,
  input  in_12,
  input  in_13,
  input  in_14,
  input  in_15,
  input  in_16,
  input  in_17,
  input  in_18,
  output out_19,
  output out_20,
  output out_21,
  output out_22,
  output out_23,
  output out_24,
  output out_25,
  output out_26,
  output out_27,
  output out_28
);

  wire alu_de_1_bit_nor_1_c_i_1, alu_de_1_bit_nor_2_c_i_1, alu_de_1_bit_nor_3_c_i_1,
       alu_de_1_bit_nor_4_c_i_1, alu_de_1_bit_nor_5_c_i_1, alu_de_1_bit_nor_6_c_i_1, alu_de_1_bit_nor_7_c_i_1;

  ALU_de_1_bit__NOR alu_de_1_bit_nor_1 (
    .A(in_3), .B(in_4), .Op(in_2), .Ci(in_1), .S(out_19), .C_i_1(alu_de_1_bit_nor_1_c_i_1));
  ALU_de_1_bit__NOR alu_de_1_bit_nor_2 (
    .A(in_5), .B(in_6), .Op(in_2), .Ci(alu_de_1_bit_nor_1_c_i_1), .S(out_20), .C_i_1(alu_de_1_bit_nor_2_c_i_1));
  ALU_de_1_bit__NOR alu_de_1_bit_nor_3 (
    .A(in_7), .B(in_8), .Op(in_2), .Ci(alu_de_1_bit_nor_2_c_i_1), .S(out_21), .C_i_1(alu_de_1_bit_nor_3_c_i_1));
  ALU_de_1_bit__NOR alu_de_1_bit_nor_4 (
    .A(in_9), .B(in_10), .Op(in_2), .Ci(alu_de_1_bit_nor_3_c_i_1), .S(out_22),
    .C_i_1(alu_de_1_bit_nor_4_c_i_1));
  ALU_de_1_bit__NOR alu_de_1_bit_nor_5 (
    .A(in_11), .B(in_12), .Op(in_2), .Ci(alu_de_1_bit_nor_4_c_i_1), .S(out_24),
    .C_i_1(alu_de_1_bit_nor_5_c_i_1));
  ALU_de_1_bit__NOR alu_de_1_bit_nor_6 (
    .A(in_13), .B(in_14), .Op(in_2), .Ci(alu_de_1_bit_nor_5_c_i_1), .S(out_25),
    .C_i_1(alu_de_1_bit_nor_6_c_i_1));
  ALU_de_1_bit__NOR alu_de_1_bit_nor_7 (
    .A(in_15), .B(in_16), .Op(in_2), .Ci(alu_de_1_bit_nor_6_c_i_1), .S(out_26),
    .C_i_1(alu_de_1_bit_nor_7_c_i_1));
  ALU_de_1_bit__NOR alu_de_1_bit_nor_8 (
    .A(in_17), .B(in_18), .Op(in_2), .Ci(alu_de_1_bit_nor_7_c_i_1), .S(out_27), .C_i_1(out_28));
  and and_1 (out_23, out_19, out_20, out_21, out_22, out_24, out_25, out_26, out_27);
endmodule

module Equivalencia_de_XOR (
  input  in_1,
  input  in_2,
  output out_3
);

  wire A_nB_out, nAB_out, not_1_out, not_2_out;

  not not_1 (not_1_out, in_1);
  not not_2 (not_2_out, in_2);
  and A_nB (A_nB_out, in_1, not_2_out);
  and nAB (nAB_out, not_1_out, in_2);
  or or_1 (out_3, A_nB_out, nAB_out);

  // Notes on the sheet:
  //   XOR = A¬B+¬AB
  //   A¬B+¬AB
endmodule
