// Logisim project Secuenciales.circ as structural Verilog: 2 circuits, main circuit 1 Contador
module _1_Contador (
  input  Comenzar_conteo,
  output [3:0] out_2
);

  wire and_1_out, j_k_ff_1_qn, j_k_ff_2_qn, j_k_ff_3_qn, RELOJ_out;

  Clock RELOJ (.out(RELOJ_out));
  J_K_Flip_Flop j_k_ff_1 (
    .J(Comenzar_conteo), .clk(RELOJ_out), .K(Comenzar_conteo), .Q(out_2[0]), .Qn(j_k_ff_1_qn));  // open: preset, en, reset
  J_K_Flip_Flop j_k_ff_2 (
    .J(Comenzar_conteo), .clk(j_k_ff_1_qn), .K(Comenzar_conteo), .Q(out_2[1]), .Qn(j_k_ff_2_qn),
    .reset(and_1_out));  // open: preset, en
  J_K_Flip_Flop j_k_ff_3 (
    .J(Comenzar_conteo), .clk(j_k_ff_2_qn), .K(Comenzar_conteo), .Q(out_2[2]), .Qn(j_k_ff_3_qn),
    .reset(and_1_out));  // open: preset, en
  J_K_Flip_Flop j_k_ff_4 (
    .J(Comenzar_conteo), .clk(j_k_ff_3_qn), .K(Comenzar_conteo), .Q(out_2[3]), .en(Comenzar_conteo),
    .reset(and_1_out));  // open: Qn, preset
  Hex_Digit_Display hex_digit_display_1 (.value(out_2));  // open: dp
  and and_1 (and_1_out, out_2[3], out_2[1]);

  // Notes on the sheet:
  //   Flip-flops
  //   Display
  //   Número en binario
endmodule

module _3_Contadores (
  input  Comenzar_conteo
);

  wire and_1_out, and_2_out, multiplexer_1_out, multiplexer_2_out, not_1_out, not_2_out, not_3_out, not_4_out;
  wire [3:0] n1_contador_1_out_2, n1_contador_2_out_2, n1_contador_3_out_2;

  not not_1 (not_1_out, n1_contador_1_out_2[1]);
  _1_Contador u_1_contador_1 (.out_2(n1_contador_1_out_2), .Comenzar_conteo(Comenzar_conteo));
  not not_2 (not_2_out, n1_contador_1_out_2[2]);
  not not_3 (not_3_out, n1_contador_2_out_2[2]);
  not not_4 (not_4_out, n1_contador_2_out_2[1]);
  and and_1 (and_1_out, n1_contador_1_out_2[0], not_1_out, not_2_out, n1_contador_1_out_2[3]);
  _1_Contador u_1_contador_2 (.out_2(n1_contador_2_out_2), .Comenzar_conteo(multiplexer_1_out));
  and and_2 (and_2_out, n1_contador_2_out_2[0], not_4_out, not_3_out, n1_contador_2_out_2[3]);
  Multiplexer #(.enable("false")) multiplexer_1 (
    .in0(1'b0), .in1(Comenzar_conteo), .out(multiplexer_1_out), .sel(and_1_out));
  _1_Contador u_1_contador_3 (.out_2(n1_contador_3_out_2), .Comenzar_conteo(multiplexer_2_out));
  Multiplexer #(.enable("false")) multiplexer_2 (
    .in0(1'b0), .in1(Comenzar_conteo), .out(multiplexer_2_out), .sel(and_2_out));
  Hex_Digit_Display hex_digit_display_1 (.value(n1_contador_3_out_2));  // open: dp
  Hex_Digit_Display hex_digit_display_2 (.value(n1_contador_1_out_2));  // open: dp
  Hex_Digit_Display hex_digit_display_3 (.value(n1_contador_2_out_2));  // open: dp
endmodule
