// Logisim project Secuenciales.circ as structural Verilog: 17 circuits, main circuit 1 Contador
module _1_Contador (
  input  Comenzar_conteo,
  output [3:0] out_2
);

  wire and_1_out, j_k_ff_1_qn, j_k_ff_2_qn, j_k_ff_3_qn, not_1_out, not_2_out, not_3_out, or_1_out, RELOJ_out;
  wire [3:0] j_k_ff_1_q;

  Clock RELOJ (.out(RELOJ_out));
  J_K_Flip_Flop j_k_ff_1 (
    .J(Comenzar_conteo), .clk(RELOJ_out), .K(Comenzar_conteo), .Q(j_k_ff_1_q[0]), .Qn(j_k_ff_1_qn));  // open: preset, en, reset
  J_K_Flip_Flop j_k_ff_2 (
    .J(Comenzar_conteo), .clk(j_k_ff_1_qn), .K(Comenzar_conteo), .Q(j_k_ff_1_q[1]), .Qn(j_k_ff_2_qn));  // open: preset, en, reset
  J_K_Flip_Flop j_k_ff_3 (
    .J(Comenzar_conteo), .clk(j_k_ff_2_qn), .K(Comenzar_conteo), .Q(j_k_ff_1_q[2]), .Qn(j_k_ff_3_qn));  // open: preset, en, reset
  J_K_Flip_Flop j_k_ff_4 (
    .J(Comenzar_conteo), .clk(j_k_ff_3_qn), .K(Comenzar_conteo), .Q(j_k_ff_1_q[3]));  // open: Qn, preset, en, reset
  Hex_Digit_Display hex_digit_display_1 (.value(out_2));  // open: dp
  not not_1 (not_1_out, j_k_ff_1_q[1]);
  not not_2 (not_2_out, j_k_ff_1_q[2]);
  not not_3 (not_3_out, j_k_ff_1_q[3]);
  or or_1 (or_1_out, and_1_out, not_3_out);
  and and_1 (and_1_out, not_1_out, not_2_out);
  Multiplexer #(.width(4), .enable("false")) multiplexer_1 (
    .in0(4'b0000), .in1(j_k_ff_1_q), .out(out_2), .sel(or_1_out));

  // Notes on the sheet:
  //   Flip-flops
  //   Display
  //   D
  //   C
  //   B
  //   A
  //   Número en binario
  //   Solo mostrar 0-9
endmodule

module _3_Contadores (
  input  Comenzar_conteo
);

  wire and_1_out, and_2_out, multiplexer_1_out, multiplexer_2_out, not_1_out, not_2_out, not_3_out, not_4_out;
  wire [3:0] n1_contador_1_out_2, n1_contador_2_out_2, n1_contador_3_out_2;

  not not_1 (not_1_out, n1_contador_1_out_2[1]);
  _1_Contador u_1_contador_1 (.out_2(n1_contador_1_out_2), .Comenzar_conteo(Comenzar_conteo));
  not not_2 (not_2_out, n1_contador_1_out_2[2]);
  not not_3 (not_3_out, n1_contador_2_out_2[2]);
  not not_4 (not_4_out, n1_contador_2_out_2[1]);
  and and_1 (and_1_out, n1_contador_1_out_2[0], not_1_out, not_2_out, n1_contador_1_out_2[3]);
  _1_Contador u_1_contador_2 (.out_2(n1_contador_2_out_2), .Comenzar_conteo(multiplexer_1_out));
  and and_2 (and_2_out, n1_contador_2_out_2[0], not_4_out, not_3_out, n1_contador_2_out_2[3]);
  Multiplexer #(.enable("false")) multiplexer_1 (
    .in0(1'b0), .in1(Comenzar_conteo), .out(multiplexer_1_out), .sel(and_1_out));
  _1_Contador u_1_contador_3 (.out_2(n1_contador_3_out_2), .Comenzar_conteo(multiplexer_2_out));
  Multiplexer #(.enable("false")) multiplexer_2 (
    .in0(1'b0), .in1(Comenzar_conteo), .out(multiplexer_2_out), .sel(and_2_out));
  Hex_Digit_Display hex_digit_display_1 (.value(n1_contador_3_out_2));  // open: dp
  Hex_Digit_Display hex_digit_display_2 (.value(n1_contador_1_out_2));  // open: dp
  Hex_Digit_Display hex_digit_display_3 (.value(n1_contador_2_out_2));  // open: dp
endmodule

module Automata_combinacional (
  input  A,
  input  E1,
  input  E2,
  output E1_2,
  output E2_2
);

  wire and_1_out, and_2_out, and_3_out, not_1_out, not_2_out, not_3_out;

  not not_1 (not_1_out, A);
  not not_2 (not_2_out, E1);
  not not_3 (not_3_out, E2);
  and and_1 (and_1_out, not_1_out, not_2_out, E2);
  and and_2 (and_2_out, A, E1);
  and and_3 (and_3_out, E1, not_3_out);
  and and_4 (E2_2, not_1_out, not_3_out);
  or or_1 (E1_2, and_1_out, and_2_out, and_3_out);

  // Notes on the sheet:
  //   T = 00
  //   TE = 01
  //   NT =10
  //   NTE = 11
endmodule

module Automata_secuencial (
  input  Entrada
);

  wire Automata_e1_2, Automata_e2_2, d_ff_1_q, d_ff_2_q, Reloj_out;

  Automata_combinacional Automata (
    .A(Entrada), .E1(d_ff_1_q), .E2(d_ff_2_q), .E1_2(Automata_e1_2), .E2_2(Automata_e2_2));
  Clock Reloj (.out(Reloj_out));
  D_Flip_Flop d_ff_1 (.clk(Reloj_out), .D(Automata_e1_2), .Q(d_ff_1_q));  // open: Qn, preset, en, reset
  D_Flip_Flop d_ff_2 (.clk(Reloj_out), .D(Automata_e2_2), .Q(d_ff_2_q));  // open: Qn, preset, en, reset

  // Notes on the sheet:
  //   Memoria
endmodule

module Registro_SR (
  input  A,
  input  B,
  input  C,
  input  D,
  input  E,
  input  F,
  input  G,
  input  H,
  input  PRENDER_APAGAR,
  output A_2,
  output B_2,
  output C_2,
  output D_2,
  output E_2,
  output F_2,
  output G_2,
  output H_2
);

  wire not_1_out, not_2_out, not_3_out, not_4_out, not_5_out, not_6_out, not_7_out, not_8_out;

  not not_1 (not_1_out, A);
  not not_2 (not_2_out, B);
  not not_3 (not_3_out, C);
  not not_4 (not_4_out, D);
  not not_5 (not_5_out, E);
  not not_6 (not_6_out, F);
  not not_7 (not_7_out, G);
  not not_8 (not_8_out, H);
  S_R_Flip_Flop s_r_ff_1 (.S(A), .clk(PRENDER_APAGAR), .R(not_1_out), .Q(A_2));  // open: Qn, preset, reset, en
  S_R_Flip_Flop s_r_ff_2 (.S(B), .clk(PRENDER_APAGAR), .R(not_2_out), .Q(B_2));  // open: Qn, preset, reset, en
  S_R_Flip_Flop s_r_ff_3 (.S(C), .clk(PRENDER_APAGAR), .R(not_3_out), .Q(C_2));  // open: Qn, preset, reset, en
  S_R_Flip_Flop s_r_ff_4 (.S(D), .clk(PRENDER_APAGAR), .R(not_4_out), .Q(D_2));  // open: Qn, preset, reset, en
  S_R_Flip_Flop s_r_ff_5 (.S(E), .clk(PRENDER_APAGAR), .R(not_5_out), .Q(E_2));  // open: Qn, preset, reset, en
  S_R_Flip_Flop s_r_ff_6 (.S(F), .clk(PRENDER_APAGAR), .R(not_6_out), .Q(F_2));  // open: Qn, preset, reset, en
  S_R_Flip_Flop s_r_ff_7 (.S(G), .clk(PRENDER_APAGAR), .R(not_7_out), .Q(G_2));  // open: Qn, preset, reset, en
  S_R_Flip_Flop s_r_ff_8 (.S(H), .clk(PRENDER_APAGAR), .R(not_8_out), .Q(H_2));  // open: Qn, preset, reset, en
endmodule

module Banco_de_registros (
  input  [1:0] Escribir_registro,
  input  [7:0] Escribir_datos,
  input  Escribir,
  input  [1:0] Leer_registro_1,
  input  [1:0] Leer_registro_2,
  output [7:0] Leer_datos_1,
  output [7:0] Leer_datos_2
);

  wire [7:0] demultiplexer_1_out0, demultiplexer_1_out1, demultiplexer_1_out2, demultiplexer_1_out3,
       Registro_0_a_2, Registro_1_a_2, Registro_2_a_2, Registro_3_a_2;

  Demultiplexer #(.select(2), .width(8), .enable("false")) demultiplexer_1 (
    .out0(demultiplexer_1_out0), .out1(demultiplexer_1_out1), .out2(demultiplexer_1_out2),
    .out3(demultiplexer_1_out3), .in(Escribir_datos), .sel(Escribir_registro));
  Registro_SR Registro_0 (
    .A(demultiplexer_1_out0[0]), .B(demultiplexer_1_out0[1]), .C(demultiplexer_1_out0[2]),
    .D(demultiplexer_1_out0[3]), .E(demultiplexer_1_out0[4]), .F(demultiplexer_1_out0[5]),
    .G(demultiplexer_1_out0[6]), .H(demultiplexer_1_out0[7]), .A_2(Registro_0_a_2[0]),
    .B_2(Registro_0_a_2[1]), .C_2(Registro_0_a_2[2]), .D_2(Registro_0_a_2[3]), .E_2(Registro_0_a_2[4]),
    .F_2(Registro_0_a_2[5]), .G_2(Registro_0_a_2[6]), .H_2(Registro_0_a_2[7]), .PRENDER_APAGAR(Escribir));
  Registro_SR Registro_1 (
    .A(demultiplexer_1_out1[0]), .B(demultiplexer_1_out1[1]), .C(demultiplexer_1_out1[2]),
    .D(demultiplexer_1_out1[3]), .E(demultiplexer_1_out1[4]), .F(demultiplexer_1_out1[5]),
    .G(demultiplexer_1_out1[6]), .H(demultiplexer_1_out1[7]), .A_2(Registro_1_a_2[0]),
    .B_2(Registro_1_a_2[1]), .C_2(Registro_1_a_2[2]), .D_2(Registro_1_a_2[3]), .E_2(Registro_1_a_2[4]),
    .F_2(Registro_1_a_2[5]), .G_2(Registro_1_a_2[6]), .H_2(Registro_1_a_2[7]), .PRENDER_APAGAR(Escribir));
  Registro_SR Registro_2 (
    .A(demultiplexer_1_out2[0]), .B(demultiplexer_1_out2[1]), .C(demultiplexer_1_out2[2]),
    .D(demultiplexer_1_out2[3]), .E(demultiplexer_1_out2[4]), .F(demultiplexer_1_out2[5]),
    .G(demultiplexer_1_out2[6]), .H(demultiplexer_1_out2[7]), .A_2(Registro_2_a_2[0]),
    .B_2(Registro_2_a_2[1]), .C_2(Registro_2_a_2[2]), .D_2(Registro_2_a_2[3]), .E_2(Registro_2_a_2[4]),
    .F_2(Registro_2_a_2[5]), .G_2(Registro_2_a_2[6]), .H_2(Registro_2_a_2[7]), .PRENDER_APAGAR(Escribir));
  Registro_SR Registro_3 (
    .A(demultiplexer_1_out3[0]), .B(demultiplexer_1_out3[1]), .C(demultiplexer_1_out3[2]),
    .D(demultiplexer_1_out3[3]), .E(demultiplexer_1_out3[4]), .F(demultiplexer_1_out3[5]),
    .G(demultiplexer_1_out3[6]), .H(demultiplexer_1_out3[7]), .A_2(Registro_3_a_2[0]),
    .B_2(Registro_3_a_2[1]), .C_2(Registro_3_a_2[2]), .D_2(Registro_3_a_2[3]), .E_2(Registro_3_a_2[4]),
    .F_2(Registro_3_a_2[5]), .G_2(Registro_3_a_2[6]), .H_2(Registro_3_a_2[7]), .PRENDER_APAGAR(Escribir));
  Multiplexer #(.select(2), .width(8), .enable("false")) multiplexer_1 (
    .in0(Registro_0_a_2), .in1(Registro_1_a_2), .in2(Registro_2_a_2), .in3(Registro_3_a_2),
    .out(Leer_datos_1), .sel(Leer_registro_1));
  Multiplexer #(.select(2), .width(8), .enable("false")) multiplexer_2 (
    .in0(Registro_0_a_2), .in1(Registro_1_a_2), .in2(Registro_2_a_2), .in3(Registro_3_a_2),
    .out(Leer_datos_2), .sel(Leer_registro_2));
endmodule

module Banco_de_registros_con_ALU_de_8_bits (
  input  ESCRIBIR,
  input  [17:0] in_2,
  output [7:0] SALIDA,
  output DESBORDAMIENTO
);

  wire [7:0] banco_de_registros_1_leer_datos_1, banco_de_registros_1_leer_datos_2, multiplexer_1_out;

  Banco_de_registros banco_de_registros_1 (
    .Escribir_registro(in_2[1:0]), .Escribir_datos(SALIDA), .Escribir(ESCRIBIR),
    .Leer_registro_1(in_2[14:13]), .Leer_registro_2(in_2[11:10]),
    .Leer_datos_1(banco_de_registros_1_leer_datos_1), .Leer_datos_2(banco_de_registros_1_leer_datos_2));
  Multiplexer #(.width(8), .enable("false")) multiplexer_1 (
    .in0(banco_de_registros_1_leer_datos_2), .in1(in_2[9:2]), .out(multiplexer_1_out), .sel(in_2[12]));
  \ALU_Final___Versión_2  \alu_final_versión_2_1  (
    .A(banco_de_registros_1_leer_datos_1), .B(multiplexer_1_out), .\Operación (in_2[17:15]),
    .Resultado(SALIDA), .Desbordamiento(DESBORDAMIENTO));

  // Notes on the sheet:
  //   ENTRADA
endmodule

module ALU_de_1_bit__Sumador (
  input  A,
  input  B,
  input  [2:0] Op,
  input  C_i,
  output S,
  output C_i_1
);

  wire A___B_____C_i_out, A___B_out, A_B_out, AB_2_out, AB_out, C_i___A___B_out;

  and AB (AB_out, A, B);
  and C_i___A___B (C_i___A___B_out, C_i, A___B_out);
  and AB_2 (AB_2_out, B, A);
  or A_B (A_B_out, A, B);
  xor A___B (A___B_out, A, B);
  Multiplexer #(.select(3), .enable("false")) multiplexer_1 (
    .in0(AB_2_out), .in1(A_B_out), .in4(A___B_____C_i_out), .out(S), .sel(Op));  // open: in2, in3, in5, in6, in7
  xor A___B_____C_i (A___B_____C_i_out, A___B_out, C_i);
  or AB__C_i___A___B (C_i_1, C_i___A___B_out, AB_out);

  // Notes on the sheet:
  //   Sumador Completo
  //   2^n entradas
  //   salida
  //   n seleccion
  //   Salida
  //   Acarreo
endmodule

module ALU_8_bits__Sumador (
  input  in_1,
  input  [2:0] Op,
  input  A,
  input  B,
  input  A_2,
  input  B_2,
  input  A_3,
  input  B_3,
  input  A_4,
  input  B_4,
  input  A_5,
  input  B_5,
  input  A_6,
  input  B_6,
  input  A_7,
  input  B_7,
  input  A_8,
  input  B_8,
  output out_19,
  output out_20,
  output out_21,
  output out_22,
  output out_23,
  output out_24,
  output out_25,
  output out_26,
  output out_27
);

  wire alu_de_1_bit_sumador_1_c_i_1, alu_de_1_bit_sumador_2_c_i_1, alu_de_1_bit_sumador_3_c_i_1,
       alu_de_1_bit_sumador_4_c_i_1, alu_de_1_bit_sumador_5_c_i_1, alu_de_1_bit_sumador_6_c_i_1,
       alu_de_1_bit_sumador_7_c_i_1;

  ALU_de_1_bit__Sumador alu_de_1_bit_sumador_1 (
    .A(A), .B(B), .Op(Op), .C_i(in_1), .S(out_19), .C_i_1(alu_de_1_bit_sumador_1_c_i_1));
  ALU_de_1_bit__Sumador alu_de_1_bit_sumador_2 (
    .A(A_2), .B(B_2), .Op(Op), .C_i(alu_de_1_bit_sumador_1_c_i_1), .S(out_20),
    .C_i_1(alu_de_1_bit_sumador_2_c_i_1));
  ALU_de_1_bit__Sumador alu_de_1_bit_sumador_3 (
    .A(A_3), .B(B_3), .Op(Op), .C_i(alu_de_1_bit_sumador_2_c_i_1), .S(out_21),
    .C_i_1(alu_de_1_bit_sumador_3_c_i_1));
  ALU_de_1_bit__Sumador alu_de_1_bit_sumador_4 (
    .A(A_4), .B(B_4), .Op(Op), .C_i(alu_de_1_bit_sumador_3_c_i_1), .S(out_22),
    .C_i_1(alu_de_1_bit_sumador_4_c_i_1));
  ALU_de_1_bit__Sumador alu_de_1_bit_sumador_5 (
    .A(A_5), .B(B_5), .Op(Op), .C_i(alu_de_1_bit_sumador_4_c_i_1), .S(out_23),
    .C_i_1(alu_de_1_bit_sumador_5_c_i_1));
  ALU_de_1_bit__Sumador alu_de_1_bit_sumador_6 (
    .A(A_6), .B(B_6), .Op(Op), .C_i(alu_de_1_bit_sumador_5_c_i_1), .S(out_24),
    .C_i_1(alu_de_1_bit_sumador_6_c_i_1));
  ALU_de_1_bit__Sumador alu_de_1_bit_sumador_7 (
    .A(A_7), .B(B_7), .Op(Op), .C_i(alu_de_1_bit_sumador_6_c_i_1), .S(out_25),
    .C_i_1(alu_de_1_bit_sumador_7_c_i_1));
  ALU_de_1_bit__Sumador alu_de_1_bit_sumador_8 (
    .A(A_8), .B(B_8), .Op(Op), .C_i(alu_de_1_bit_sumador_7_c_i_1), .S(out_26), .C_i_1(out_27));

  // Notes on the sheet:
  //   B
  //   Desbordamiento aritmetico
endmodule

module \ALU_de_1_bit__Sustracción  (
  input  A,
  input  B,
  input  [2:0] Op,
  input  C_i,
  output S,
  output C_i_1
);

  wire A___B___C_i_out, and_1_out, and_2_out, and_3_out, C_i_B_out, nAB_out, nAC_i_out, not_1_out, or_1_out,
       or_2_out, or_3_out, xor_1_out, xor_2_out;

  not not_1 (not_1_out, A);
  and and_1 (and_1_out, A, B);
  and nAB (nAB_out, not_1_out, B);
  and nAC_i (nAC_i_out, not_1_out, C_i);
  and and_2 (and_2_out, C_i, xor_1_out);
  and C_i_B (C_i_B_out, C_i, B);
  and and_3 (and_3_out, B, A);
  or or_1 (or_1_out, A, B);
  xor xor_1 (xor_1_out, A, B);
  Multiplexer #(.select(3), .enable("false")) multiplexer_1 (
    .in0(and_3_out), .in1(or_1_out), .in4(xor_2_out), .in5(A___B___C_i_out), .out(S), .sel(Op));  // open: in2, in3, in6, in7
  xor xor_2 (xor_2_out, xor_1_out, C_i);
  or or_2 (or_2_out, and_2_out, and_1_out);
  Multiplexer #(.select(3), .enable("false")) multiplexer_2 (
    .in4(or_2_out), .in5(or_3_out), .out(C_i_1), .sel(Op));  // open: in0, in1, in2, in3, in6, in7
  ExactlyOne A___B___C_i (.out(A___B___C_i_out), .in0(C_i), .in2(B), .in4(A));
  or or_3 (or_3_out, C_i_B_out, nAC_i_out, nAB_out);

  // Notes on the sheet:
  //   Sustraendo = B
  //   Minuendo = A
  //   Sumador Completo
  //   Restador Completo
  //   Bit prestado = C(i)
  //   2^n entradas
  //   salida
  //   n seleccion
  //   Salida
  //   Diferencia
  //   Prestamo
endmodule

module \ALU_8_bits__Sustracción  (
  input  in_1,
  input  [2:0] Op,
  input  in_3,
  input  in_4,
  input  in_5,
  input  in_6,
  input  in_7,
  input  in_8,
  input  in_9,
  input  in_10,
  input  in_11,
  input  in_12,
  input  in_13,
  input  in_14,
  input  in_15,
  input  in_16,
  input  in_17,
  input  in_18,
  output out_19,
  output out_20,
  output out_21,
  output out_22,
  output out_23,
  output out_24,
  output out_25,
  output out_26,
  output out_27,
  output out_28
);

  wire \alu_de_1_bit_sustracción_con_igualdad_1_s , \alu_de_1_bit_sustracción_con_igualdad_2_s ,
       \alu_de_1_bit_sustracción_con_igualdad_3_s , \alu_de_1_bit_sustracción_con_igualdad_4_s ,
       \alu_de_1_bit_sustracción_con_igualdad_5_s , \alu_de_1_bit_sustracción_con_igualdad_6_s ,
       \alu_de_1_bit_sustracción_con_igualdad_7_s , \alu_de_1_bit_sustracción_con_igualdad_8_s ;

  \ALU_de_1_bit__Sustracción_con_igualdad  \alu_de_1_bit_sustracción_con_igualdad_1  (
    .A(in_3), .B(in_4), .Op(Op), .Ci(in_1), .S(\alu_de_1_bit_sustracción_con_igualdad_1_s ), .C_i_1(out_19));
  \ALU_de_1_bit__Sustracción_con_igualdad  \alu_de_1_bit_sustracción_con_igualdad_2  (
    .A(in_5), .B(in_6), .Op(Op), .Ci(\alu_de_1_bit_sustracción_con_igualdad_1_s ),
    .S(\alu_de_1_bit_sustracción_con_igualdad_2_s ), .C_i_1(out_20));
  \ALU_de_1_bit__Sustracción_con_igualdad  \alu_de_1_bit_sustracción_con_igualdad_3  (
    .A(in_7), .B(in_8), .Op(Op), .Ci(\alu_de_1_bit_sustracción_con_igualdad_2_s ),
    .S(\alu_de_1_bit_sustracción_con_igualdad_3_s ), .C_i_1(out_21));
  \ALU_de_1_bit__Sustracción_con_igualdad  \alu_de_1_bit_sustracción_con_igualdad_4  (
    .A(in_9), .B(in_10), .Op(Op), .Ci(\alu_de_1_bit_sustracción_con_igualdad_3_s ),
    .S(\alu_de_1_bit_sustracción_con_igualdad_4_s ), .C_i_1(out_22));
  \ALU_de_1_bit__Sustracción_con_igualdad  \alu_de_1_bit_sustracción_con_igualdad_5  (
    .A(in_11), .B(in_12), .Op(Op), .Ci(\alu_de_1_bit_sustracción_con_igualdad_4_s ),
    .S(\alu_de_1_bit_sustracción_con_igualdad_5_s ), .C_i_1(out_24));
  \ALU_de_1_bit__Sustracción_con_igualdad  \alu_de_1_bit_sustracción_con_igualdad_6  (
    .A(in_13), .B(in_14), .Op(Op), .Ci(\alu_de_1_bit_sustracción_con_igualdad_5_s ),
    .S(\alu_de_1_bit_sustracción_con_igualdad_6_s ), .C_i_1(out_25));
  \ALU_de_1_bit__Sustracción_con_igualdad  \alu_de_1_bit_sustracción_con_igualdad_7  (
    .A(in_15), .B(in_16), .Op(Op), .Ci(\alu_de_1_bit_sustracción_con_igualdad_6_s ),
    .S(\alu_de_1_bit_sustracción_con_igualdad_7_s ), .C_i_1(out_26));
  \ALU_de_1_bit__Sustracción_con_igualdad  \alu_de_1_bit_sustracción_con_igualdad_8  (
    .A(in_17), .B(in_18), .Op(Op), .Ci(\alu_de_1_bit_sustracción_con_igualdad_7_s ),
    .S(\alu_de_1_bit_sustracción_con_igualdad_8_s ), .C_i_1(out_27));
  Multiplexer #(.select(3), .enable("false")) multiplexer_1 (
    .in4(\alu_de_1_bit_sustracción_con_igualdad_8_s ), .out(out_28), .sel(Op));  // open: in0, in1, in2, in3, in5, in6, in7
  and and_1 (out_23, out_19, out_20, out_21, out_22, out_24, out_25, out_26, out_27);

  // Notes on the sheet:
  //   Desbordamiento aritmetico
  //   0 no son iguales/ 1 son iguales
endmodule

module \ALU_de_1_bit__Sustracción_con_igualdad  (
  input  A,
  input  B,
  input  [2:0] Op,
  input  Ci,
  output S,
  output C_i_1
);

  wire A___B_out, and_1_out, and_2_out, and_3_out, and_4_out, and_5_out, and_6_out, not_1_out, not_2_out,
       or_1_out, or_2_out, or_3_out, xor_1_out, xor_2_out, xor_3_out;

  not not_1 (not_1_out, A);
  and and_1 (and_1_out, A, B);
  and and_2 (and_2_out, not_1_out, B);
  and and_3 (and_3_out, not_1_out, Ci);
  and and_4 (and_4_out, Ci, xor_1_out);
  and and_5 (and_5_out, Ci, B);
  and and_6 (and_6_out, B, A);
  or or_1 (or_1_out, A, B);
  xor xor_1 (xor_1_out, A, B);
  Multiplexer #(.select(3), .enable("false")) multiplexer_1 (
    .in0(and_6_out), .in1(or_1_out), .in3(not_2_out), .in4(xor_2_out), .in5(xor_3_out), .out(S), .sel(Op));  // open: in2, in6, in7
  xor xor_2 (xor_2_out, xor_1_out, Ci);
  or or_2 (or_2_out, and_4_out, and_1_out);
  xor A___B (A___B_out, A, B);
  Multiplexer #(.select(3), .enable("false")) multiplexer_2 (
    .in4(or_2_out), .in5(or_3_out), .out(C_i_1), .sel(Op));  // open: in0, in1, in2, in3, in6, in7
  ExactlyOne xor_3 (.out(xor_3_out), .in0(Ci), .in2(B), .in4(A));
  or or_3 (or_3_out, and_5_out, and_3_out, and_2_out);
  not not_2 (not_2_out, A___B_out);

  // Notes on the sheet:
  //   Sumador Completo
  //   Igualdad
  //   Restador Completo
  //   2^n entradas
  //   salida
  //   n seleccion
  //   Salida
endmodule

module ALU_de_1_bit__NOR (
  input  A,
  input  B,
  input  [2:0] Op,
  input  Ci,
  output S,
  output C_i_1
);

  wire and_1_out, and_2_out, and_3_out, and_4_out, and_5_out, and_6_out, nA_nB_out, not_1_out, not_2_out,
       not_3_out, not_4_out, or_1_out, or_2_out, or_3_out, xor_1_out, xor_2_out, xor_3_out, xor_4_out;

  not not_1 (not_1_out, A);
  and and_1 (and_1_out, A, B);
  and and_2 (and_2_out, not_1_out, B);
  and and_3 (and_3_out, not_1_out, Ci);
  and and_4 (and_4_out, Ci, xor_1_out);
  and and_5 (and_5_out, Ci, B);
  not not_2 (not_2_out, A);
  not not_3 (not_3_out, B);
  and and_6 (and_6_out, B, A);
  or or_1 (or_1_out, A, B);
  xor xor_1 (xor_1_out, A, B);
  and nA_nB (nA_nB_out, not_2_out, not_3_out);
  Multiplexer #(.select(3), .enable("false")) multiplexer_1 (
    .in0(and_6_out), .in1(or_1_out), .in2(nA_nB_out), .in3(not_4_out), .in4(xor_2_out), .in5(xor_4_out),
    .out(S), .sel(Op));  // open: in6, in7
  xor xor_2 (xor_2_out, xor_1_out, Ci);
  or or_2 (or_2_out, and_4_out, and_1_out);
  xor xor_3 (xor_3_out, A, B);
  Multiplexer #(.select(3), .enable("false")) multiplexer_2 (
    .in4(or_2_out), .in5(or_3_out), .out(C_i_1), .sel(Op));  // open: in0, in1, in2, in3, in6, in7
  ExactlyOne xor_4 (.out(xor_4_out), .in0(Ci), .in2(B), .in4(A));
  or or_3 (or_3_out, and_5_out, and_3_out, and_2_out);
  not not_4 (not_4_out, xor_3_out);

  // Notes on the sheet:
  //   Sumador Completo
  //   Restador Completo
  //   NOR
  //   2^n entradas
  //   salida
  //   n seleccion
  //   Salida
  //   Igualdad
endmodule

module ALU_8_bits_Final (
  input  in_1,
  input  [2:0] in_2,
  input  in_3,
  input  in_4,
  input  in_5,
  input  in_6,
  input  in_7,
  input  in_8,
  input  in_9,
  input  in_10,
  input  in_11,
  input  in_12,
  input  in_13,
  input  in_14,
  input  in_15,
  input  in_16,
  input  in_17,
  input  in_18,
  output out_19,
  output out_20,
  output out_21,
  output out_22,
  output out_23,
  output out_24,
  output out_25,
  output out_26,
  output out_27,
  output Desbordamiento
);

  wire alu_de_1_bit_nor_1_c_i_1, alu_de_1_bit_nor_2_c_i_1, alu_de_1_bit_nor_3_c_i_1,
       alu_de_1_bit_nor_4_c_i_1, alu_de_1_bit_nor_5_c_i_1, alu_de_1_bit_nor_6_c_i_1,
       alu_de_1_bit_nor_7_c_i_1, alu_de_1_bit_nor_8_c_i_1;

  ALU_de_1_bit__NOR alu_de_1_bit_nor_1 (
    .A(in_3), .B(in_4), .Op(in_2), .Ci(in_1), .S(out_19), .C_i_1(alu_de_1_bit_nor_1_c_i_1));
  ALU_de_1_bit__NOR alu_de_1_bit_nor_2 (
    .A(in_5), .B(in_6), .Op(in_2), .Ci(alu_de_1_bit_nor_1_c_i_1), .S(out_20), .C_i_1(alu_de_1_bit_nor_2_c_i_1));
  ALU_de_1_bit__NOR alu_de_1_bit_nor_3 (
    .A(in_7), .B(in_8), .Op(in_2), .Ci(alu_de_1_bit_nor_2_c_i_1), .S(out_21), .C_i_1(alu_de_1_bit_nor_3_c_i_1));
  ALU_de_1_bit__NOR alu_de_1_bit_nor_4 (
    .A(in_9), .B(in_10), .Op(in_2), .Ci(alu_de_1_bit_nor_3_c_i_1), .S(out_22),
    .C_i_1(alu_de_1_bit_nor_4_c_i_1));
  ALU_de_1_bit__NOR alu_de_1_bit_nor_5 (
    .A(in_11), .B(in_12), .Op(in_2), .Ci(alu_de_1_bit_nor_4_c_i_1), .S(out_24),
    .C_i_1(alu_de_1_bit_nor_5_c_i_1));
  ALU_de_1_bit__NOR alu_de_1_bit_nor_6 (
    .A(in_13), .B(in_14), .Op(in_2), .Ci(alu_de_1_bit_nor_5_c_i_1), .S(out_25),
    .C_i_1(alu_de_1_bit_nor_6_c_i_1));
  ALU_de_1_bit__NOR alu_de_1_bit_nor_7 (
    .A(in_15), .B(in_16), .Op(in_2), .Ci(alu_de_1_bit_nor_6_c_i_1), .S(out_26),
    .C_i_1(alu_de_1_bit_nor_7_c_i_1));
  ALU_de_1_bit__NOR alu_de_1_bit_nor_8 (
    .A(in_17), .B(in_18), .Op(in_2), .Ci(alu_de_1_bit_nor_7_c_i_1), .S(out_27),
    .C_i_1(alu_de_1_bit_nor_8_c_i_1));
  Multiplexer #(.select(3), .enable("false")) multiplexer_1 (
    .in4(alu_de_1_bit_nor_8_c_i_1), .out(Desbordamiento), .sel(in_2));  // open: in0, in1, in2, in3, in5, in6, in7
  and and_1 (out_23, out_19, out_20, out_21, out_22, out_24, out_25, out_26, out_27);
endmodule

module ALU_Final (
  input  [7:0] A,
  input  [7:0] B,
  input  [2:0] \Operación ,
  output [7:0] Resultado,
  output Desbordamiento
);

  wire [7:0] alu_8_bits_final_1_out_19;
  wire [7:7] alu_8_bits_final_1_out_23;

  ALU_8_bits_Final alu_8_bits_final_1 (
    .in_3(A[0]), .in_4(B[0]), .in_5(A[1]), .in_6(B[1]), .in_7(A[2]), .in_8(B[2]), .in_9(A[3]), .in_10(B[3]),
    .in_11(A[4]), .in_12(B[4]), .in_13(A[5]), .in_14(B[5]), .in_15(A[6]), .in_16(B[6]), .in_17(A[7]),
    .in_18(B[7]), .out_19(alu_8_bits_final_1_out_19[0]), .out_20(alu_8_bits_final_1_out_19[1]),
    .out_21(alu_8_bits_final_1_out_19[2]), .out_22(alu_8_bits_final_1_out_19[3]),
    .out_23(alu_8_bits_final_1_out_23[7]), .out_24(alu_8_bits_final_1_out_19[4]),
    .out_25(alu_8_bits_final_1_out_19[5]), .out_26(alu_8_bits_final_1_out_19[6]),
    .out_27(alu_8_bits_final_1_out_19[7]), .in_1(1'b0), .in_2(\Operación ), .Desbordamiento(Desbordamiento));
  Multiplexer #(.select(3), .width(8), .enable("false")) multiplexer_1 (
    .in0(alu_8_bits_final_1_out_19), .in1(alu_8_bits_final_1_out_19), .in2(alu_8_bits_final_1_out_19),
    .in3({8{alu_8_bits_final_1_out_23[7]}}), .in4(alu_8_bits_final_1_out_19),
    .in5(alu_8_bits_final_1_out_19), .out(Resultado), .sel(\Operación ));  // open: in6, in7
endmodule

module \ALU_Final___Versión_2  (
  input  [7:0] A,
  input  [7:0] B,
  input  [2:0] \Operación ,
  output [7:0] Resultado,
  output Desbordamiento
);

  ALU_Final alu_final_1 (
    .A(A), .B(B), .\Operación (\Operación ), .Resultado(Resultado), .Desbordamiento(Desbordamiento));

  // Notes on the sheet:
  //   000 = AND
  //   001 = OR
  //   010 = NOR
  //   011 = IGUALDAD
  //   100 = ADICIÓN
  //   101 = SUSTRACCIÓN
endmodule

module Equivalencia_de_XOR (
  input  in_1,
  input  in_2,
  output out_3
);

  wire A_nB_out, nAB_out, not_1_out, not_2_out;

  not not_1 (not_1_out, in_1);
  not not_2 (not_2_out, in_2);
  and A_nB (A_nB_out, in_1, not_2_out);
  and nAB (nAB_out, not_1_out, in_2);
  or or_1 (out_3, A_nB_out, nAB_out);

  // Notes on the sheet:
  //   XOR = A¬B+¬AB
  //   A¬B+¬AB
endmodule
